# Fritzing sketch hvac (saved by Fritzing 0.8.5b)
breadboards: 1

parts:
  Arduino_Dueminalove_/_Uno = Arduino Uno (Rev3)
  U1 = LCD-16X2 [package=lcd-16x2]
  R1 = Rotary Potentiometer (Small) [maximum_resistance=10kΩ package=THT]
  S1 = Toggle Switch [part_number="3-way switch with center neutral" package=THT]
  U3 = RELAY-2 [package=relay-g5v]
  Q1 = NPN-Transistor [part_number=2N2222A package="TO92 [THT]"]
  D1 = Rectifier Diode [part_number=1N4004 package="300 mil [THT]"]
  J1 = Screw terminal - 2 pins [part_number="RTD PT1000 Sensor" package=THT]
  J2 = Screw terminal - 2 pins [part_number="To Burner Temp switch" package=THT]
  R2 = Resistor [tolerance=±5% resistance=10k package=THT]
  R3 = Resistor [tolerance=±5% resistance=100k package=THT]
  R4 = Resistor [tolerance=±5% resistance=8.2k package=THT]
  R5 = Resistor [tolerance=±5% resistance=47k package=THT]
  R6 = Resistor [tolerance=±5% resistance=8.2k package=THT]
  R7 = Resistor [tolerance=±5% resistance=47k package=THT]
  R8 = Resistor [tolerance=±5% resistance=1k package=THT]
  R9 = Resistor [tolerance=±5% resistance=10k package=THT]
  R10 = Resistor [tolerance=±5% resistance=10k package=THT]
  R11 = Resistor [tolerance=±5% resistance=10k package=THT]
  U4 = LM324N [package=DIP14]

nets:
  N1: Arduino_Dueminalove_/_Uno.A0, R5.Pin_1, U4.4O
  N2: Arduino_Dueminalove_/_Uno.A1, R1.leg2
  N3: Arduino_Dueminalove_/_Uno.D11_PWM/MOSI, U1.E
  N4: Arduino_Dueminalove_/_Uno.D12/MISO, U1.RS
  N5: Arduino_Dueminalove_/_Uno.D13/SCK, R8.Pin_1
  GND: Arduino_Dueminalove_/_Uno.GND, U1.VSS, U1.VO, U1.R_W, U1.K, Q1.E, J1.pin1, R7.Pin_1, R9.Pin_1, R10.Pin_0, R11.Pin_0, U4.3+, U4.GND
  N6: Arduino_Dueminalove_/_Uno.D2, U1.DB7
  N7: Arduino_Dueminalove_/_Uno.D3_PWM, U1.DB6
  N8: Arduino_Dueminalove_/_Uno.D4, U1.DB5
  N9: Arduino_Dueminalove_/_Uno.D5_PWM, U1.DB4
  N10: Arduino_Dueminalove_/_Uno.D6_PWM, S1.L2, R11.Pin_1
  N11: Arduino_Dueminalove_/_Uno.D7, S1.L1, R10.Pin_1
  5V: Arduino_Dueminalove_/_Uno.5V, U1.VDD, U1.A, R1.wiper, S1.COM, R2.Pin_0, R3.Pin_1, U4.Vcc+
  N12: Arduino_Dueminalove_/_Uno.VIN, U3.2, D1.cathode
  N13: U3.5, J2.pin1
  N14: U3.9, Q1.C, D1.anode
  N15: U3.10, J2.pin2
  N16: Q1.B, R8.Pin_0
  N17: J1.pin2, R2.Pin_1, U4.2+
  N18: R3.Pin_0, R9.Pin_0, U4.1+
  N19: R4.Pin_0, R5.Pin_0, U4.4-
  N20: R4.Pin_1, U4.1O, U4.1-
  N21: R6.Pin_0, U4.2-, U4.2O
  N22: R6.Pin_1, R7.Pin_0, U4.4+
  N23: U4.3O, U4.3-

notes:
  Work in progress!
  2013-12-27
  OpAmp circuitry for RTD readings within 1.1Vref range for maximum accuracy

custom parts:
  LM324N: Low Power Quad Operational Amplifiers
